# Fritzing sketch solar2heater (saved by Fritzing 0.9.3b)
circuit board: 7.25419cm x 6.05312cm
breadboards: 1

parts:
  TFT = lcd color display 1.3in 240x240 7pin interface [package=THT]
  Rled = Resistor [tolerance=±5% resistance=220 package=THT]
  button = Pushbutton [package="[THT]"]
  LED1 = LED - 5mm [color="Red (633nm)" package="5 mm [THT]"]
  Raspberry_Pi_1 = Raspberry Pi 3 [part_number=RPI-3-V1.2]
  Rled_2 = Resistor [tolerance=±5% resistance=220 package=THT]
  LED3 = LED - 5mm [color="Red (633nm)" package="5 mm [THT]"]
  buzzer = KY-012 Active Buzzer Module [package="Breakout board"]
  opto = IC, DIP package, 4 pins [chip_label=IC]
  teleinfo = Terminal 2pin
  Ropto = Resistor [tolerance=±5% resistance=220 package=THT]
  serial = female pin header, 5 pins [form="♀ (female)"]
  pullup = Resistor [tolerance=±5% resistance=220 package=THT]
  current = INA219 High Side DC Current Sensor Breakout [part_number=904]
  J1 = female pin header, 2 pins [form="♀ (female)"]
  J2 = female pin header, 2 pins [form="♀ (female)"]
  gesture = APDS-9960 RGB and Gesture Sensor [part_number=SEN-12787]
  Fuel = SparkFun LiPo Fuel Gauge [part_number=TOL-10617]
  temp = mystery part, 4 pins [chip_label="BME 280" part_number="BME 280"]
  lux = mystery part, 4 pins [chip_label=tsl2561 part_number=lux]
  i2c = mystery part, 4 pins [chip_label=i2c part_number=i2c]

nets:
  GND: TFT.GND, Rled.Pin_1, button.Pin_1, button.Pin_2, Raspberry_Pi_1.GND, Rled_2.Pin_1, buzzer.-, opto.pin1, serial.pin1, current.GND, gesture.GND, Fuel.GND, temp.pin3, lux.pin3, i2c.pin4
  3.3V: TFT.VCC, Raspberry_Pi_1.3v3, Raspberry_Pi_1.3V3, serial.pin5, pullup.Pin_1, current.VCC, J1.pin1, J2.pin1, gesture.VCC, Fuel.VCC, temp.pin4, lux.pin4, i2c.pin3
  N1: TFT.SCL, Raspberry_Pi_1.GIPO11
  N2: TFT.SDA, Raspberry_Pi_1.GIPO10
  N3: TFT.RES, Raspberry_Pi_1.GIPO13
  N4: TFT.DC, Raspberry_Pi_1.GIPO19
  N5: TFT.BLK, Raspberry_Pi_1.GIPO26
  N6: Rled.Pin_0, LED1.anode
  N7: button.Pin_3, button.Pin_4, Raspberry_Pi_1.GIPO20
  N8: LED1.cathode, Raspberry_Pi_1.GIPO12
  N9: Raspberry_Pi_1.GPIO2, current.SDA, gesture.SDA, Fuel.SDA, temp.pin1, lux.pin1, i2c.pin2
  N10: Raspberry_Pi_1.GPIO3, current.SCL, gesture.SCL, Fuel.SCL, temp.pin2, lux.pin2, i2c.pin1
  N11: Raspberry_Pi_1.GIPO17, J1.pin2
  N12: Raspberry_Pi_1.GIPO27, J2.pin2
  N13: Raspberry_Pi_1.GIPO21, buzzer.S
  N14: Raspberry_Pi_1.GIPO24, LED3.cathode
  N15: Raspberry_Pi_1.GIPO15, opto.pin2, serial.pin3, pullup.Pin_0
  N16: Raspberry_Pi_1.GIPO14, serial.pin2
  N17: Raspberry_Pi_1.5V, serial.pin4
  N18: Rled_2.Pin_0, LED3.anode
  N19: opto.pin3, Ropto.Pin_0
  N20: opto.pin4, teleinfo.pin_1
  N21: teleinfo.pin_2, Ropto.Pin_1

notes:
  meaudre robotics

custom parts:
  lcd color display 1.3in 240x240 7pin interface: 1.3 Inch Color 240 x 240 IPS TFT LCD Display Screen Module Board 7 Pin 4 Wire ST7789VW Drive IC SPI interface.
  KY-012 Active Buzzer Module: Active Piezoelectric Buzzer Module KY-012, it produces single-tone sound when signal is high. (Special thanks to vanepp for fixing the PCB holes and other errors)
  Terminal 2pin: 2-pin Terminal Block
  INA219 High Side DC Current Sensor Breakout: This breakout board will solve all your power-monitoring problems. Instead of struggling with two multimeters, you can just use the handy INA219B chip on this breakout to both measure both the high side voltage and DC current draw over I2C with 1% precision. Most current-measuring devices such as our current panel meter are only good for low side measuring. That means that unless you want to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
  APDS-9960 RGB and Gesture Sensor: Breakout board for the Avago APDS-9960 proximity, light, RGB, and gesture sensors. Please visit www.sparkfun.com to learn more.
  SparkFun LiPo Fuel Gauge: LiPo batteries are a great way to power your projects. They’re small, lightweight, and pack a pretty good punch for their size. Unfortunately, even the best batteries eventually run low on power and when they do it’s often unexpected (and at the worst time). Don’t be caught by surprise next time your board suddenly powers-down! The SparkFun LiPo Fuel Gauge connects your battery to your project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
